# Fritzing sketch control_galpon (saved by Fritzing 0.9.2b)
breadboards: 1

parts:
  Parte1 = Arduino Uno (Rev3)
  U1 = 2.4GHz Low Power Transceiver [package=qfn20]
  Tiny_RTC1 = Tiny RTC
  KY-3 = Keyes Relay [package=THT]
  R1 = Resistor [tolerance=±5% resistance=220 package=THT]
  T1 = ds18x20 OneWire termometre [package="TO92 [THT]"]
  KY-4 = Keyes Relay [package=THT]
  KY-5 = Keyes Relay [package=THT]
  KY-6 = Keyes Relay [package=THT]

nets:
  N1: Parte1.D8, R1.Pin_1, T1.DQ
  N2: Parte1.D9_PWM, U1.CE
  N3: Parte1.D10_PWM/SS, U1.CSN
  N4: Parte1.D11_PWM/MOSI, U1.MOSI
  N5: Parte1.D12/MISO, U1.MISO
  N6: Parte1.D13/SCK, U1.SCK
  GND: Parte1.GND, U1.VSS, Tiny_RTC1.GND, KY-3.ground, T1.GND, KY-4.ground, KY-5.ground, KY-6.ground
  N7: Parte1.A4/SDA, Tiny_RTC1.SDA
  N8: Parte1.A5/SCL, Tiny_RTC1.SCL
  N9: Parte1.D2, Tiny_RTC1.SQ
  N10: Parte1.D3_PWM, Tiny_RTC1.DS
  N11: Parte1.D4, KY-3.signal
  N12: Parte1.D5_PWM, KY-6.signal
  N13: Parte1.D6_PWM, KY-4.signal
  N14: Parte1.D7, KY-5.signal
  3V3: Parte1.3V3, U1.VDD
  5V: Parte1.5V, Tiny_RTC1.VCC, KY-3.power, R1.Pin_0, KY-4.power, KY-5.power, KY-6.power

custom parts:
  Tiny RTC: Tiny RTC I2C module DS1370Z RTC and AT24C32 EEPROM
  Keyes Relay: The Keyes 5V relay module is suitable for SCM development, home appliance control. It uses a 5V~12V TIL control signal which can control DC / AC signal.
  ds18x20 OneWire termometre: A ds18b20 o ds18s20 digital termometre with OneWire protocol comunication
